// Digital circuit CPU.dig as structural Verilog
// The RUN1920 CPU component
module CPU (
  input  [31:0] DATABUS_IN,
  input  CLOCK,
  input  nRESET,
  output nRE,
  output nWE,
  output HALTED,
  output [31:0] ADDRESSBUS_OUT,
  output [31:0] DATABUS_OUT
);

  wire ALU_carry_out, ALU_negative, ALU_overflow, ALU_zero, FlagRegisterBank_p8, FlagRegisterBank_p9,
       FlagRegisterBank_p10, FlagRegisterBank_p11, InstructionDecoder_halt, InstructionDecoder_loadhi,
       InstructionDecoder_pop, InstructionDecoder_push, InstructionDecoder_setflags,
       InstructionDecoder_use_constant, not_1_out, not_2_out, or_1_out, Tester_testsucceeds, Timer_execute,
       Timer_fetch, Timer_nreset_out;
  wire [2:0] InstructionDecoder_opcode;
  wire [3:0] InstructionDecoder_addr_a, InstructionDecoder_addr_b, InstructionDecoder_addr_dest,
       InstructionDecoder_condition;
  wire [31:0] ALU_result, dec4a_1_q, InstructionDecoder_constant, multiplexer_1_out, multiplexer_2_out,
       multiplexer_3_out, multiplexer_4_out, multiplexer_5_out, RegisterBank_reg_a, RegisterBank_reg_b;

  InstructionDecoder InstructionDecoder (
    .INSTRUCTION(DATABUS_IN), .CLOCK(CLOCK), .EXECUTE(Timer_execute), .FETCH(Timer_fetch),
    .nRESET(Timer_nreset_out), .nWRITE(nWE), .PUSH(InstructionDecoder_push), .nREAD(nRE),
    .POP(InstructionDecoder_pop), .ADDR_DEST(InstructionDecoder_addr_dest),
    .ADDR_B(InstructionDecoder_addr_b), .ADDR_A(InstructionDecoder_addr_a),
    .CONSTANT(InstructionDecoder_constant), .LOADHI(InstructionDecoder_loadhi),
    .USE_CONSTANT(InstructionDecoder_use_constant), .OPCODE(InstructionDecoder_opcode),
    .SetFlags(InstructionDecoder_setflags), .CONDITION(InstructionDecoder_condition),
    .HALT(InstructionDecoder_halt));
  Timer Timer (
    .HALT(InstructionDecoder_halt), .CLOCK(CLOCK), .nRESET_IN(nRESET), .TEST_SUCCEEDS(Tester_testsucceeds),
    .EXECUTE(Timer_execute), .FETCH(Timer_fetch), .nRESET_OUT(Timer_nreset_out), .HALTED(HALTED));
  Multiplexer #(.Bits(32)) multiplexer_1 (
    .sel(InstructionDecoder_loadhi), .in_0(multiplexer_2_out), .in_1(InstructionDecoder_constant),
    .out(multiplexer_1_out));
  RegisterBank RegisterBank (
    .DATA(multiplexer_1_out), .POP(InstructionDecoder_pop), .ADDR_DEST(InstructionDecoder_addr_dest),
    .ADDR_B(InstructionDecoder_addr_b), .ADDR_A(InstructionDecoder_addr_a), .nRESET(Timer_nreset_out),
    .CLOCK(CLOCK), .REG_B(RegisterBank_reg_b), .REG_A(RegisterBank_reg_a));
  or or_1 (or_1_out, nWE, nRE);
  Multiplexer #(.Bits(32)) multiplexer_2 (
    .sel(or_1_out), .in_0(ALU_result), .in_1(multiplexer_3_out), .out(multiplexer_2_out));
  not not_1 (not_1_out, InstructionDecoder_push);
  Multiplexer #(.Bits(32)) multiplexer_3 (
    .sel(not_1_out), .in_0(dec4a_1_q), .in_1(DATABUS_IN), .out(multiplexer_3_out));
  Dec4A dec4a_1 (.D(RegisterBank_reg_b), .Q(dec4a_1_q));
  Multiplexer #(.Bits(32)) multiplexer_4 (
    .sel(InstructionDecoder_use_constant), .in_0(RegisterBank_reg_a), .in_1(InstructionDecoder_constant),
    .out(multiplexer_4_out));
  ALU ALU (
    .B(RegisterBank_reg_b), .A(multiplexer_4_out), .OPCODE(InstructionDecoder_opcode), .RESULT(ALU_result),
    .Overflow(ALU_overflow), .Negative(ALU_negative), .Carry_out(ALU_carry_out), .Zero(ALU_zero));
  Multiplexer #(.Bits(32)) multiplexer_5 (
    .sel(not_2_out), .in_0(dec4a_1_q), .in_1(ALU_result), .out(multiplexer_5_out));
  // FlagRegisterBank FlagRegisterBank: pin names not known; wires that end beside it: ALU_overflow, ALU_negative, ALU_carry_out, ALU_zero, InstructionDecoder_setflags, Timer_nreset_out, CLOCK, FlagRegisterBank_p8, FlagRegisterBank_p9, FlagRegisterBank_p10, FlagRegisterBank_p11
  not not_2 (not_2_out, InstructionDecoder_push);
  Multiplexer #(.Bits(32)) multiplexer_6 (
    .sel(or_1_out), .in_0({32{1'b0}}), .in_1(multiplexer_5_out), .out(ADDRESSBUS_OUT));
  Multiplexer #(.Bits(32)) multiplexer_7 (.sel(nWE), .in_0({32{1'b0}}), .in_1(RegisterBank_reg_a), .out(DATABUS_OUT));
  Tester Tester (
    .Overflow(FlagRegisterBank_p8), .Negative(FlagRegisterBank_p9), .Carry(FlagRegisterBank_p10),
    .Zero(FlagRegisterBank_p11), .Condition(InstructionDecoder_condition), .TestSucceeds(Tester_testsucceeds));
endmodule
